// Logisim project proj1-alu.circ as structural Verilog: 8 circuits, main circuit main
module main (
  input  [7:0] A,
  input  [7:0] B,
  input  [2:0] Opcode,
  output [7:0] O,
  output Cout
);

  wire c4, c5, c6;
  wire [7:0] r1, r2, r3, r4, r5, r6, r7;

  assign r1 = A ^ B;  // XOR_Gate xor_1, 8 bits wide
  assign r2 = A & B;  // AND_Gate and_1, 8 bits wide
  assign r3 = A | B;  // OR_Gate or_1, 8 bits wide
  Adder8 adder8_1 (.A(A), .B(B), .Cin(1'b0), .S(r4), .Cout(c4));
  Subtractor8 subtractor8_1 (.A(A), .B(B), .D(r5), .Cout(c5));
  ShiftRight shiftright_1 (.B(B), .O(r6), .Cout(c6));
  Multiplier4x4 multiplier4x4_1 (.A(A), .B(B), .P(r7));
  Mux8to1_8bit mux8to1_8bit_1 (
    .I0(B), .I1(r1), .I2(r2), .I3(r3), .I4(r4), .I5(r5), .I6(r6), .I7(r7), .Sel(Opcode), .Out(O));
  Mux8to1_1bit mux8to1_1bit_1 (
    .I0(1'b0), .I1(1'b0), .I2(1'b0), .I3(1'b0), .I4(c4), .I5(c5), .I6(c6), .I7(1'b0), .Sel(Opcode), .Out(Cout));
endmodule

module FullAdder (
  input  a,
  input  b,
  input  cin,
  output s,
  output cout
);

  wire g, p, x;

  xor xor_1 (x, a, b);
  and and_1 (g, a, b);
  and and_2 (p, x, cin);
  xor xor_2 (s, x, cin);
  or or_1 (cout, g, p);
endmodule

module Adder8 (
  input  [7:0] A,
  input  [7:0] B,
  input  Cin,
  output [7:0] S,
  output Cout
);

  wire c1, c2, c3, c4, c5, c6, c7;

  FullAdder fulladder_1 (.a(A[0]), .b(B[0]), .cin(Cin), .s(S[0]), .cout(c1));
  FullAdder fulladder_2 (.a(A[4]), .b(B[4]), .cin(c4), .s(S[4]), .cout(c5));
  FullAdder fulladder_3 (.a(A[1]), .b(B[1]), .cin(c1), .s(S[1]), .cout(c2));
  FullAdder fulladder_4 (.a(A[5]), .b(B[5]), .cin(c5), .s(S[5]), .cout(c6));
  FullAdder fulladder_5 (.a(A[2]), .b(B[2]), .cin(c2), .s(S[2]), .cout(c3));
  FullAdder fulladder_6 (.a(A[6]), .b(B[6]), .cin(c6), .s(S[6]), .cout(c7));
  FullAdder fulladder_7 (.a(A[3]), .b(B[3]), .cin(c3), .s(S[3]), .cout(c4));
  FullAdder fulladder_8 (.a(A[7]), .b(B[7]), .cin(c7), .s(S[7]), .cout(Cout));

  // Other names for the same wires on the sheet: c0 = Cin; c8 = Cout
endmodule

module Subtractor8 (
  input  [7:0] A,
  input  [7:0] B,
  output [7:0] D,
  output Cout
);

  wire [7:0] nB;

  assign nB = ~B;  // NOT_Gate not_1, 8 bits wide
  Adder8 adder8_1 (.A(A), .B(nB), .Cin(1'b1), .S(D), .Cout(Cout));
endmodule

module ShiftRight (
  input  [7:0] B,
  output [7:0] O,
  output Cout
);


  assign Cout = B[0];
  assign O = {1'b0, B[7:1]};
endmodule

module Multiplier4x4 (
  input  [7:0] A,
  input  [7:0] B,
  output [7:0] P
);

  wire pp0_0, pp0_1, pp0_2, pp0_3, pp1_0, pp1_1, pp1_2, pp1_3, pp2_0, pp2_1, pp2_2, pp2_3, pp3_0, pp3_1,
       pp3_2, pp3_3;
  wire [7:0] S1, S2;

  and and_1 (pp0_0, A[0], B[0]);
  and and_2 (pp0_1, A[0], B[1]);
  and and_3 (pp0_2, A[0], B[2]);
  and and_4 (pp0_3, A[0], B[3]);
  and and_5 (pp1_0, A[1], B[0]);
  and and_6 (pp1_1, A[1], B[1]);
  and and_7 (pp1_2, A[1], B[2]);
  and and_8 (pp1_3, A[1], B[3]);
  Adder8 adder8_1 (
    .A({4'b0000, pp3_0, pp2_0, pp1_0, pp0_0}), .B({3'b000, pp3_1, pp2_1, pp1_1, pp0_1, 1'b0}), .Cin(1'b0),
    .S(S1));  // open: Cout
  and and_9 (pp2_0, A[2], B[0]);
  and and_10 (pp2_1, A[2], B[1]);
  and and_11 (pp2_2, A[2], B[2]);
  and and_12 (pp2_3, A[2], B[3]);
  and and_13 (pp3_0, A[3], B[0]);
  and and_14 (pp3_1, A[3], B[1]);
  and and_15 (pp3_2, A[3], B[2]);
  and and_16 (pp3_3, A[3], B[3]);
  Adder8 adder8_2 (.A(S1), .B({2'b00, pp3_2, pp2_2, pp1_2, pp0_2, 2'b00}), .Cin(1'b0), .S(S2));  // open: Cout
  Adder8 adder8_3 (.A(S2), .B({1'b0, pp3_3, pp2_3, pp1_3, pp0_3, 3'b000}), .Cin(1'b0), .S(P));  // open: Cout

  // Other names for the same wires on the sheet: W0[3:0] = {pp3_0, pp2_0, pp1_0, pp0_0};
  //   W1[4:1] = {pp3_1, pp2_1, pp1_1, pp0_1}; W2[5:2] = {pp3_2, pp2_2, pp1_2, pp0_2};
  //   W3[6:3] = {pp3_3, pp2_3, pp1_3, pp0_3}
endmodule

module Mux8to1_8bit (
  input  [7:0] I0,
  input  [7:0] I1,
  input  [7:0] I2,
  input  [7:0] I3,
  input  [7:0] I4,
  input  [7:0] I5,
  input  [7:0] I6,
  input  [7:0] I7,
  input  [2:0] Sel,
  output [7:0] Out
);

  wire d0, d1, d2, d3, d4, d5, d6, d7;
  wire [7:0] e0, e1, e2, e3, e4, e5, e6, e7, m0, m1, m2, m3, m4, m5, m6, m7;

  Decoder #(.select(3), .enable("false")) decoder_1 (
    .out0(d0), .out1(d1), .out2(d2), .out3(d3), .out4(d4), .out5(d5), .out6(d6), .out7(d7), .sel(Sel));
  assign m0 = I0 & e0;  // AND_Gate and_1, 8 bits wide
  assign m1 = I1 & e1;  // AND_Gate and_2, 8 bits wide
  assign m2 = I2 & e2;  // AND_Gate and_3, 8 bits wide
  assign m3 = I3 & e3;  // AND_Gate and_4, 8 bits wide
  assign m4 = I4 & e4;  // AND_Gate and_5, 8 bits wide
  assign m5 = I5 & e5;  // AND_Gate and_6, 8 bits wide
  assign m6 = I6 & e6;  // AND_Gate and_7, 8 bits wide
  assign m7 = I7 & e7;  // AND_Gate and_8, 8 bits wide
  assign e0 = {{7{d0}}, d0};  // Bit_Extender bit_extender_1
  assign e1 = {{7{d1}}, d1};  // Bit_Extender bit_extender_2
  assign e2 = {{7{d2}}, d2};  // Bit_Extender bit_extender_3
  assign e3 = {{7{d3}}, d3};  // Bit_Extender bit_extender_4
  assign e4 = {{7{d4}}, d4};  // Bit_Extender bit_extender_5
  assign e5 = {{7{d5}}, d5};  // Bit_Extender bit_extender_6
  assign e6 = {{7{d6}}, d6};  // Bit_Extender bit_extender_7
  assign e7 = {{7{d7}}, d7};  // Bit_Extender bit_extender_8
  assign Out = m0 | m1 | m2 | m3 | m4 | m5 | m6 | m7;  // OR_Gate or_1, 8 bits wide
endmodule

module Mux8to1_1bit (
  input  I0,
  input  I1,
  input  I2,
  input  I3,
  input  I4,
  input  I5,
  input  I6,
  input  I7,
  input  [2:0] Sel,
  output Out
);

  wire d0, d1, d2, d3, d4, d5, d6, d7, m0, m1, m2, m3, m4, m5, m6, m7;

  Decoder #(.select(3), .enable("false")) decoder_1 (
    .out0(d0), .out1(d1), .out2(d2), .out3(d3), .out4(d4), .out5(d5), .out6(d6), .out7(d7), .sel(Sel));
  and and_1 (m0, I0, d0);
  and and_2 (m1, I1, d1);
  and and_3 (m2, I2, d2);
  and and_4 (m3, I3, d3);
  and and_5 (m4, I4, d4);
  and and_6 (m5, I5, d5);
  and and_7 (m6, I6, d6);
  and and_8 (m7, I7, d7);
  or or_1 (Out, m0, m1, m2, m3, m4, m5, m6, m7);
endmodule
